// Logisim project ALU 8 bit.circ as structural Verilog
// ALU 8 BIT
module ALU_8_bits (
  input  [7:0] Operand_B,
  input  [7:0] Operand_A,
  input  [2:0] Operation,
  output Cout_ADD,
  output Zero,
  output [7:0] Result_0,
  output Cout_SUB
);

  wire [2:0] bit_extender_1_out;
  wire [7:0] adder_1_out, adder_2_out, not_1_out, shifter_1_out;

  assign not_1_out = ~Operand_B;  // NOT_Gate not_1, 8 bits wide
  Bit_Extender #(.out_width(3)) bit_extender_1 (.in(Operand_B), .out(bit_extender_1_out));
  Adder adder_1 (.a(Operand_B), .b(Operand_A), .out(adder_1_out), .cout(Cout_ADD));  // open: cin
  Adder adder_2 (.a(Operand_A), .b(not_1_out), .out(adder_2_out), .cin(1'b1), .cout(Cout_SUB));
  Shifter shifter_1 (.in(Operand_A), .\dist (bit_extender_1_out), .out(shifter_1_out));
  Multiplexer #(.select(3), .width(8)) multiplexer_1 (
    .in0(adder_1_out), .in1(adder_2_out), .in2(adder_1_out), .in3(adder_1_out), .in4(adder_1_out),
    .in5(adder_2_out), .in7(shifter_1_out), .out(Result_0), .sel(Operation));  // open: in6, en
  nor nor_1 (Zero, Result_0[0], Result_0[1], Result_0[2], Result_0[3], Result_0[4], Result_0[5], Result_0[6], Result_0[7]);
endmodule
