// Logisim project Control Unit.circ as structural Verilog: 1 circuit, main circuit Control Unit
module Control_Unit (
  input  [2:0] ALU_opcode,
  output I___R__INTO__RS,
  output Reg_Write,
  output [1:0] R___I___Shift_Select_ALU,
  output Beq_ALU_input_Control,
  output Jump_control,
  output BEQ_Control,
  output sw,
  output lw,
  output Select_lw___sw,
  output Select_result_from_ALU__Memory
);

  wire undriven;

  Multiplexer #(.select(3)) multiplexer_1 (
    .in0(1'b0), .in1(1'b0), .in2(1'b1), .in3(1'b1), .in4(1'b1), .in5(1'b1), .in7(1'b0),
    .out(I___R__INTO__RS), .sel(ALU_opcode));  // open: in6, en
  Multiplexer #(.select(3)) multiplexer_2 (
    .in0(1'b1), .in1(1'b1), .in2(1'b1), .in3(1'b1), .in4(1'b0), .in5(1'b0), .in7(1'b1), .out(Reg_Write),
    .sel(ALU_opcode));  // open: in6, en
  Multiplexer #(.select(3)) multiplexer_3 (
    .in0(1'b0), .in1(1'b0), .in2(1'b0), .in3(1'b0), .in4(1'b0), .in5(1'b0), .in7(1'b1),
    .out(R___I___Shift_Select_ALU[1]), .sel(ALU_opcode));  // open: in6, en
  Multiplexer #(.select(3)) multiplexer_4 (
    .in0(1'b0), .in1(1'b0), .in2(1'b1), .in3(1'b1), .in4(1'b1), .in5(1'b1), .in7(1'b0),
    .out(R___I___Shift_Select_ALU[0]), .sel(ALU_opcode));  // open: in6, en
  Multiplexer #(.select(3)) multiplexer_5 (
    .in0(1'b0), .in1(1'b0), .in2(1'b0), .in3(1'b0), .in4(1'b0), .in5(1'b1), .in7(1'b0),
    .out(Beq_ALU_input_Control), .sel(ALU_opcode));  // open: in6, en
  Multiplexer #(.select(3)) multiplexer_6 (
    .in0(1'b0), .in1(1'b0), .in2(1'b0), .in3(1'b0), .in4(1'b0), .in5(1'b0), .in6(1'b1), .in7(1'b0),
    .out(Jump_control), .sel(ALU_opcode));  // open: en
  Multiplexer #(.select(3)) multiplexer_7 (
    .in0(1'b0), .in1(1'b0), .in2(1'b0), .in3(1'b0), .in4(1'b0), .in5(1'b1), .in6(1'b0), .in7(1'b0),
    .out(BEQ_Control), .sel(ALU_opcode), .en(undriven));
  Multiplexer #(.select(3)) multiplexer_8 (
    .in0(1'b0), .in1(1'b0), .in2(1'b0), .in3(1'b0), .in4(1'b1), .in5(1'b0), .in6(1'b0), .in7(1'b0), .out(sw),
    .sel(ALU_opcode));  // open: en
  Multiplexer #(.select(3)) multiplexer_9 (
    .in0(1'b0), .in1(1'b0), .in2(1'b0), .in3(1'b1), .in4(1'b0), .in5(1'b0), .in6(1'b0), .in7(1'b0), .out(lw),
    .sel(ALU_opcode));  // open: en
  Multiplexer #(.select(3)) multiplexer_10 (
    .in0(1'b0), .in1(1'b0), .in2(1'b0), .in3(1'b1), .in4(1'b1), .in5(1'b0), .in6(1'b0), .in7(1'b0),
    .out(Select_lw___sw), .sel(ALU_opcode));  // open: en
  Multiplexer #(.select(3)) multiplexer_11 (
    .in0(1'b0), .in1(1'b0), .in2(1'b0), .in3(1'b1), .in4(1'b0), .in5(1'b0), .in6(1'b0), .in7(1'b0),
    .out(Select_result_from_ALU__Memory), .sel(ALU_opcode));  // open: en
endmodule
