// Logisim project Datapath.circ as structural Verilog: 4 circuits, main circuit main
module main (
  input  [2:0] in_1,
  input  Clear_Reg,
  input  C_in,
  input  Clear_Mem,
  output Jump_control,
  output BEQ_control,
  output [4:0] Jump,
  output [2:0] op,
  output [1:0] RS,
  output [1:0] RD,
  output [2:0] Immi,
  output Zero,
  output Reg_Write,
  output Cout_Add,
  output [7:0] R_Data1,
  output C_out_Sub,
  output [7:0] out_17,
  output [7:0] Res_Adr_Lw_Sw,
  output [7:0] Res__Mem_Data,
  output I___R_into_RS,
  output [1:0] R___I___Shift_Select,
  output beq_ALU_input,
  output Sw,
  output Lw,
  output Select_lw_sw,
  output Select_result_from_ALU__Memory
);

  wire and_1_out, Clock_out;
  wire [0:0] demultiplexer_1_out0;
  wire [2:0] demultiplexer_1_out1;
  wire [7:0] adder_1_out, adder_2_out, bit_extender_1_out, bit_extender_2_out, multiplexer_1_out,
       multiplexer_3_out, multiplexer_4_out, PC_q, ram_1_data, reg_file_1_data02, shifter_1_out;

  Control_Unit control_unit_1 (
    .I___R__INTO__RS(I___R_into_RS), .ALU_opcode(op), .Reg_Write(Reg_Write),
    .R___I___Shift_Select_ALU(R___I___Shift_Select), .Beq_ALU_input_Control(beq_ALU_input),
    .Jump_control(Jump_control), .BEQ_Control(BEQ_control), .sw(Sw), .lw(Lw), .Select_lw___sw(Select_lw_sw),
    .Select_result_from_ALU__Memory(Select_result_from_ALU__Memory));
  Register PC (.D(multiplexer_3_out), .Q(PC_q), .clk(Clock_out));  // open: en, clr
  Clock Clock (.out(Clock_out));
  Adder adder_1 (.a(PC_q), .b(8'h1), .out(adder_1_out));  // open: cin, cout
  ROM rom_1 (.addr(PC_q), .data({op, Jump[4:3], Immi}));  // open: sel
  Demultiplexer #(.width(3), .enable("false")) demultiplexer_1 (
    .out0({RS, demultiplexer_1_out0[0]}), .out1(demultiplexer_1_out1), .in(Immi), .sel(I___R_into_RS));
  assign bit_extender_1_out = {{7{1'b0}}, demultiplexer_1_out0[0]};  // Bit_Extender bit_extender_1
  assign bit_extender_2_out = {{5{1'b0}}, demultiplexer_1_out1};  // Bit_Extender bit_extender_2
  Reg_file reg_file_1 (
    .Data_IN(Res__Mem_Data), .Reg_Write(Reg_Write), .Data01(R_Data1), .RD_Data_Address(Jump[4:3]), .RS(RS),
    .Data02(reg_file_1_data02), .Clear_Data(Clear_Reg), .Clock(Clock_out));
  Shifter shifter_1 (.in(bit_extender_2_out), .\dist (in_1), .out(shifter_1_out));
  Multiplexer #(.width(8), .enable("false")) multiplexer_1 (
    .in0(bit_extender_2_out), .in1(reg_file_1_data02), .out(multiplexer_1_out), .sel(beq_ALU_input));
  Multiplexer #(.select(2), .width(8), .enable("false")) multiplexer_2 (
    .in0(reg_file_1_data02), .in1(multiplexer_1_out), .in2(bit_extender_1_out), .out(out_17),
    .sel(R___I___Shift_Select));  // open: in3
  Adder adder_2 (.a(adder_1_out), .b(shifter_1_out), .out(adder_2_out));  // open: cin, cout
  ALU_8_bits alu_8_bits_1 (
    .Operand_B(R_Data1), .Operand_A(out_17), .Cout_ADD(Cout_Add), .Zero(Zero), .Result_0(Res_Adr_Lw_Sw),
    .Cout_SUB(C_out_Sub), .Operation(op), .C_in(C_in));
  Multiplexer #(.width(8), .enable("false")) multiplexer_3 (
    .in0(multiplexer_4_out), .in1({adder_1_out[7:5], Jump[4:3], Immi}), .out(multiplexer_3_out),
    .sel(Jump_control));
  Multiplexer #(.width(8), .enable("false")) multiplexer_4 (
    .in0(adder_1_out), .in1(adder_2_out), .out(multiplexer_4_out), .sel(and_1_out));
  and and_1 (and_1_out, Zero, BEQ_control);
  RAM #(.bus("separate")) ram_1 (
    .addr(Res_Adr_Lw_Sw), .din(reg_file_1_data02), .data(ram_1_data), .str(Sw), .sel(Select_lw_sw),
    .clk(Clock_out), .ld(Lw), .clr(Clear_Mem));
  Multiplexer #(.width(8), .enable("false")) multiplexer_5 (
    .in0(Res_Adr_Lw_Sw), .in1(ram_1_data), .out(Res__Mem_Data), .sel(Select_result_from_ALU__Memory));

  assign Jump[2:0] = Immi;
  assign RD = Jump[4:3];

  // Notes on the sheet:
  //   INSTRUCTION MEMORY
  //   Sajid Ahmed 
  //   For Jump
  //   Shift Ammount
  //   Immidiate
  //   BEQ
  //   DATA MEMORY
endmodule

module Reg_file (
  input  [7:0] Data_IN,
  input  Reg_Write,
  input  [1:0] RD_Data_Address,
  input  [1:0] RS,
  input  Clock,
  input  Clear_Data,
  output [7:0] Data01,
  output [7:0] Data02
);

  wire and_1_out, and_2_out, and_3_out, and_4_out, decoder_1_out0, decoder_1_out1, decoder_1_out2,
       decoder_1_out3;
  wire [7:0] AC_q, s1_q, s2_q, s3_q;

  Decoder #(.select(2)) decoder_1 (
    .out0(decoder_1_out0), .out1(decoder_1_out1), .out2(decoder_1_out2), .out3(decoder_1_out3),
    .sel(RD_Data_Address));  // open: en
  and and_1 (and_1_out, Reg_Write, decoder_1_out0);
  and and_2 (and_2_out, Reg_Write, decoder_1_out1);
  and and_3 (and_3_out, Reg_Write, decoder_1_out2);
  and and_4 (and_4_out, Reg_Write, decoder_1_out3);
  Register AC (.D(Data_IN), .en(and_1_out), .Q(AC_q), .clk(Clock), .clr(Clear_Data));
  Register s1 (.D(Data_IN), .en(and_2_out), .Q(s1_q), .clk(Clock), .clr(Clear_Data));
  Register s2 (.D(Data_IN), .en(and_3_out), .Q(s2_q), .clk(Clock), .clr(Clear_Data));
  Register s3 (.D(Data_IN), .en(and_4_out), .Q(s3_q), .clk(Clock), .clr(Clear_Data));
  Multiplexer #(.select(2), .width(8)) multiplexer_1 (
    .in0(AC_q), .in1(s1_q), .in2(s2_q), .in3(s3_q), .out(Data01), .sel(RS));  // open: en
  Multiplexer #(.select(2), .width(8)) multiplexer_2 (
    .in0(AC_q), .in1(s1_q), .in2(s2_q), .in3(s3_q), .out(Data02), .sel(RD_Data_Address));  // open: en
endmodule

module ALU_8_bits (
  input  C_in,
  input  [7:0] Operand_B,
  input  [7:0] Operand_A,
  input  [2:0] Operation,
  output Cout_ADD,
  output Zero,
  output [7:0] Result_0,
  output Cout_SUB
);

  wire [2:0] bit_extender_1_out;
  wire [7:0] adder_1_out, adder_2_out, not_1_out, shifter_1_out;

  assign not_1_out = ~Operand_B;  // NOT_Gate not_1, 8 bits wide
  Bit_Extender #(.out_width(3)) bit_extender_1 (.in(Operand_A), .out(bit_extender_1_out));
  Adder adder_1 (.a(Operand_B), .b(Operand_A), .out(adder_1_out), .cin(C_in), .cout(Cout_ADD));
  Adder adder_2 (.a(Operand_A), .b(not_1_out), .out(adder_2_out), .cin(1'b1), .cout(Cout_SUB));
  Shifter shifter_1 (.in(Operand_B), .\dist (bit_extender_1_out), .out(shifter_1_out));
  Multiplexer #(.select(3), .width(8)) multiplexer_1 (
    .in0(adder_1_out), .in1(adder_2_out), .in2(adder_1_out), .in3(adder_1_out), .in4(adder_1_out),
    .in5(adder_2_out), .in7(shifter_1_out), .out(Result_0), .sel(Operation));  // open: in6, en
  nor nor_1 (Zero, Result_0[0], Result_0[1], Result_0[2], Result_0[3], Result_0[4], Result_0[5], Result_0[6], Result_0[7]);
endmodule

module Control_Unit (
  input  [2:0] ALU_opcode,
  output I___R__INTO__RS,
  output Reg_Write,
  output [1:0] R___I___Shift_Select_ALU,
  output Beq_ALU_input_Control,
  output Jump_control,
  output BEQ_Control,
  output sw,
  output lw,
  output Select_lw___sw,
  output Select_result_from_ALU__Memory
);

  wire undriven;

  Multiplexer #(.select(3)) multiplexer_1 (
    .in0(1'b0), .in1(1'b0), .in2(1'b1), .in3(1'b1), .in4(1'b1), .in5(1'b1), .in7(1'b0),
    .out(I___R__INTO__RS), .sel(ALU_opcode));  // open: in6, en
  Multiplexer #(.select(3)) multiplexer_2 (
    .in0(1'b1), .in1(1'b1), .in2(1'b1), .in3(1'b1), .in4(1'b0), .in5(1'b0), .in7(1'b1), .out(Reg_Write),
    .sel(ALU_opcode));  // open: in6, en
  Multiplexer #(.select(3)) multiplexer_3 (
    .in0(1'b0), .in1(1'b0), .in2(1'b0), .in3(1'b0), .in4(1'b0), .in5(1'b0), .in7(1'b1),
    .out(R___I___Shift_Select_ALU[1]), .sel(ALU_opcode));  // open: in6, en
  Multiplexer #(.select(3)) multiplexer_4 (
    .in0(1'b0), .in1(1'b0), .in2(1'b1), .in3(1'b1), .in4(1'b1), .in5(1'b1), .in7(1'b0),
    .out(R___I___Shift_Select_ALU[0]), .sel(ALU_opcode));  // open: in6, en
  Multiplexer #(.select(3)) multiplexer_5 (
    .in0(1'b0), .in1(1'b0), .in2(1'b0), .in3(1'b0), .in4(1'b0), .in5(1'b1), .in7(1'b0),
    .out(Beq_ALU_input_Control), .sel(ALU_opcode));  // open: in6, en
  Multiplexer #(.select(3)) multiplexer_6 (
    .in0(1'b0), .in1(1'b0), .in2(1'b0), .in3(1'b0), .in4(1'b0), .in5(1'b0), .in6(1'b1), .in7(1'b0),
    .out(Jump_control), .sel(ALU_opcode));  // open: en
  Multiplexer #(.select(3)) multiplexer_7 (
    .in0(1'b0), .in1(1'b0), .in2(1'b0), .in3(1'b0), .in4(1'b0), .in5(1'b1), .in6(1'b0), .in7(1'b0),
    .out(BEQ_Control), .sel(ALU_opcode), .en(undriven));
  Multiplexer #(.select(3)) multiplexer_8 (
    .in0(1'b0), .in1(1'b0), .in2(1'b0), .in3(1'b0), .in4(1'b1), .in5(1'b0), .in6(1'b0), .in7(1'b0), .out(sw),
    .sel(ALU_opcode));  // open: en
  Multiplexer #(.select(3)) multiplexer_9 (
    .in0(1'b0), .in1(1'b0), .in2(1'b0), .in3(1'b1), .in4(1'b0), .in5(1'b0), .in6(1'b0), .in7(1'b0), .out(lw),
    .sel(ALU_opcode));  // open: en
  Multiplexer #(.select(3)) multiplexer_10 (
    .in0(1'b0), .in1(1'b0), .in2(1'b0), .in3(1'b1), .in4(1'b1), .in5(1'b0), .in6(1'b0), .in7(1'b0),
    .out(Select_lw___sw), .sel(ALU_opcode));  // open: en
  Multiplexer #(.select(3)) multiplexer_11 (
    .in0(1'b0), .in1(1'b0), .in2(1'b0), .in3(1'b1), .in4(1'b0), .in5(1'b0), .in6(1'b0), .in7(1'b0),
    .out(Select_result_from_ALU__Memory), .sel(ALU_opcode));  // open: en
endmodule
