// Logisim project Register File(8 bit).circ as structural Verilog: 2 circuits, main circuit main
// CPU
module main (
  input  Reg_Write,
  input  [1:0] RS,
  input  [1:0] RD,
  input  [7:0] Write_Data_in_RD,
  output [7:0] Read_Data_from_RS,
  output [7:0] Read_Data_from_RT
);

  wire Clock_out;

  Clock Clock (.out(Clock_out));
  Register_File register_file_1 (
    .Data_IN(Write_Data_in_RD), .Data01(Read_Data_from_RS), .Data02(Read_Data_from_RT), .Data_Address(RD),
    .RS(RS), .Reg_Write(Reg_Write), .Clock(Clock_out));
endmodule

module Register_File (
  input  [7:0] Data_IN,
  input  Reg_Write,
  input  [1:0] Data_Address,
  input  [1:0] RS,
  input  Clock,
  output [7:0] Data01,
  output [7:0] Data02
);

  wire and_1_out, and_2_out, and_3_out, and_4_out, decoder_1_out0, decoder_1_out1, decoder_1_out2,
       decoder_1_out3;
  wire [7:0] register_1_q, register_2_q, register_3_q, register_4_q;

  Decoder #(.select(2)) decoder_1 (
    .out0(decoder_1_out0), .out1(decoder_1_out1), .out2(decoder_1_out2), .out3(decoder_1_out3),
    .sel(Data_Address));  // open: en
  and and_1 (and_1_out, Reg_Write, decoder_1_out0);
  and and_2 (and_2_out, Reg_Write, decoder_1_out1);
  and and_3 (and_3_out, Reg_Write, decoder_1_out2);
  and and_4 (and_4_out, Reg_Write, decoder_1_out3);
  Register register_1 (.D(Data_IN), .en(and_1_out), .Q(register_1_q), .clk(Clock));  // open: clr
  Register register_2 (.D(Data_IN), .en(and_2_out), .Q(register_2_q), .clk(Clock));  // open: clr
  Register register_3 (.D(Data_IN), .en(and_3_out), .Q(register_3_q), .clk(Clock));  // open: clr
  Register register_4 (.D(Data_IN), .en(and_4_out), .Q(register_4_q), .clk(Clock));  // open: clr
  Multiplexer #(.select(2), .width(8)) multiplexer_1 (
    .in0(register_1_q), .in1(register_2_q), .in2(register_3_q), .in3(register_4_q), .out(Data01), .sel(RS));  // open: en
  Multiplexer #(.select(2), .width(8)) multiplexer_2 (
    .in0(register_1_q), .in1(register_2_q), .in2(register_3_q), .in3(register_4_q), .out(Data02),
    .sel(Data_Address));  // open: en
endmodule
